# Fritzing sketch LaserHarp (saved by Fritzing 0.9.0b)
breadboards: 1

parts:
  IC1 = L293D [package=THT]
  Part1 = Arduino Uno (Rev3)
  M1 = Stepper Motor - Unipolar
  Laser = LEDs [package=led10mm]
  R1 = Resistor [package="2512 [SMD]"]

nets:
  N1: IC1.Enable_1, IC1.Enable_2, IC1.+V, Part1.5V
  N2: IC1.In_1, Part1.D9_PWM
  N3: IC1.Out_1_(_Controlled_by_Enable_1_), M1.A
  N4: IC1.0V, Part1.GND, Laser.A
  N5: IC1.Out_2_(_Controlled_by_Enable_1_), M1.C
  N6: IC1.In_2, Part1.D8
  N7: IC1.In_3, Part1.D11_PWM/MOSI
  N8: IC1.Out_3_(_Controlled_by_Enable_2_), M1.D
  N9: IC1.Out_4_(_Controlled_by_Enable_2_), M1.B
  N10: IC1.In_4, Part1.D10_PWM/SS
  N11: Part1.D6_PWM, R1.Pin_1
  N12: Laser.C, R1.Pin_0
